// Logisim project noise_generator.circ as structural Verilog: 1 circuit, main circuit main
module main (
  input  rgb,
  input  reset
);

  wire counter_1_carry, counter_2_carry, random_1_p2, rgb_video_1_p1, rgb_video_1_p4;
  wire [7:0] counter_1_q, counter_2_q;

  Counter counter_1 (
    .count(rgb_video_1_p4), .Q(counter_1_q), .carry(counter_1_carry), .clk(random_1_p2), .clr(reset));  // open: load, D, up
  Counter counter_2 (
    .count(counter_1_carry), .Q(counter_2_q), .carry(counter_2_carry), .clk(random_1_p2), .clr(reset));  // open: load, D, up
  // Random random_1: pin names not known; wires that end beside it: rgb, random_1_p2
  Clock clock_1 (.out(random_1_p2));
  // RGB_Video #(.height(256), .scale(1), .width(256)) rgb_video_1: pin names not known; wires that end beside it: rgb_video_1_p1, reset, random_1_p2, rgb_video_1_p4, counter_1_q, counter_2_q, rgb_video_1_p1
  not not_1 (rgb_video_1_p4, counter_2_carry);
endmodule
